// Logisim project ULA.circ as structural Verilog: 1 circuit, main circuit main
module main (
  input  [7:0] A,
  input  [7:0] B,
  input  [2:0] S,
  output [7:0] F
);

  wire [7:0] adder_1_out, and_1_out, nand_1_out, nor_1_out, or_1_out, subtractor_1_out, xnor_1_out, xor_1_out;

  Adder adder_1 (.a(A), .b(B), .out(adder_1_out));  // open: cin, cout
  Subtractor subtractor_1 (.a(A), .b(B), .out(subtractor_1_out));  // open: bin, bout
  assign and_1_out = A & B;  // AND_Gate and_1, 8 bits wide
  assign or_1_out = A | B;  // OR_Gate or_1, 8 bits wide
  assign xor_1_out = A ^ B;  // XOR_Gate xor_1, 8 bits wide
  assign nand_1_out = ~(A & B);  // NAND_Gate nand_1, 8 bits wide
  assign nor_1_out = ~(A | B);  // NOR_Gate nor_1, 8 bits wide
  assign xnor_1_out = ~(A ^ B);  // XNOR_Gate xnor_1, 8 bits wide
  Multiplexer #(.select(3), .width(8)) multiplexer_1 (
    .in0(adder_1_out), .in1(subtractor_1_out), .in2(and_1_out), .in3(or_1_out), .in4(xor_1_out),
    .in5(nand_1_out), .in6(nor_1_out), .in7(xnor_1_out), .out(F), .sel(S));

  // Notes on the sheet:
  //   ENTRADA
  //   PROJETO DE UMA UNIDADE LÓGICA ARITIMÉTICA (ULA)
  //   MULTIPLEXADOR
  //   8 X 1
  //   SELETOR
  //   SAIDA
endmodule
