// Logisim project SOMA.circ as structural Verilog: 1 circuit, main circuit main
module main (
  input  [7:0] A,
  input  [7:0] B,
  output [7:0] S
);

  Adder adder_1 (.a(A), .b(B), .out(S));  // open: cin, cout

  // Notes on the sheet:
  //   SOMA
endmodule
