// Logisim project SUBT.circ as structural Verilog: 1 circuit, main circuit main
module main (
  input  [7:0] A,
  input  [7:0] B,
  output [7:0] S
);

  Subtractor subtractor_1 (.a(A), .b(B), .out(S));  // open: bin, bout

  // Notes on the sheet:
  //   SUB
endmodule
