// Logisim project OR.circ as structural Verilog: 1 circuit, main circuit main
module main (
  input  [7:0] A,
  input  [7:0] B,
  output [7:0] S
);

  assign S = A | B;  // OR_Gate or_1, 8 bits wide

  // Notes on the sheet:
  //   OR8
endmodule
