// Logisim project XNOR.circ as structural Verilog: 1 circuit, main circuit main
module main (
  input  [7:0] A,
  input  [7:0] B,
  output [7:0] S
);

  assign S = ~(A ^ B);  // XNOR_Gate xnor_1, 8 bits wide

  // Notes on the sheet:
  //   XNOR8
endmodule
