// Logisim project PROJETO.circ.circ as structural Verilog
module Soma (
  input  [7:0] A,
  input  [7:0] B,
  output [7:0] out_3
);

  Adder adder_1 (.a(A), .b(B), .out(out_3));  // open: cin, cout

  // Notes on the sheet:
  //   OPERADOR DA SOMA
  //   SOMA
endmodule

module Subtracao (
  input  [7:0] A,
  input  [7:0] B,
  output [7:0] out_3
);

  Subtractor subtractor_1 (.a(A), .b(B), .out(out_3));  // open: bin, bout

  // Notes on the sheet:
  //   OPERADOR DA SUBTRACAO
  //   SUB
  //   DIFERENCA
endmodule

module AND8 (
  input  [7:0] A,
  input  [7:0] B,
  output [7:0] AND8
);

  assign AND8 = A & B;  // AND_Gate and_1, 8 bits wide

  // Notes on the sheet:
  //   PORTA LOGICA AND
endmodule

module OR8 (
  input  [7:0] A,
  input  [7:0] B,
  output [7:0] out_3
);

  assign out_3 = A | B;  // OR_Gate or_1, 8 bits wide

  // Notes on the sheet:
  //   PORTA LOGICA OR
  //   OR8
endmodule

module XOR8 (
  input  [7:0] A,
  input  [7:0] B,
  output [7:0] out_3
);

  assign out_3 = A ^ B;  // XOR_Gate xor_1, 8 bits wide

  // Notes on the sheet:
  //   PORTA LOGICA XOR
  //   XOR8
endmodule

module NAND8 (
  input  [7:0] in_1,
  input  [7:0] in_2,
  output [7:0] out_3
);

  assign out_3 = ~(in_1 & in_2);  // NAND_Gate nand_1, 8 bits wide

  // Notes on the sheet:
  //   PORTA LOGICA NAND
  //   NAND8
endmodule

module NOR8 (
  input  [7:0] in_1,
  input  [7:0] in_2,
  output [7:0] out_3
);

  assign out_3 = ~(in_1 | in_2);  // NOR_Gate nor_1, 8 bits wide

  // Notes on the sheet:
  //   PORTA LOGICA NOR
  //   NOR8
endmodule

module XNOR8 (
  input  [7:0] in_1,
  input  [7:0] in_2,
  output [7:0] out_3
);

  assign out_3 = ~(in_1 ^ in_2);  // XNOR_Gate xnor_1, 8 bits wide

  // Notes on the sheet:
  //   PORTA LOGICA XNOR
  //   XNOR8
endmodule

module MUX8x1 (
  input  [7:0] A,
  input  [7:0] B,
  input  [2:0] SELETOR,
  output [7:0] SAIDA
);

  wire [7:0] adder_1_out, and_1_out, nand_1_out, nor_1_out, or_1_out, subtractor_1_out, xnor_1_out, xor_1_out;

  Adder adder_1 (.a(A), .b(B), .out(adder_1_out));  // open: cin, cout
  Subtractor subtractor_1 (.a(A), .b(B), .out(subtractor_1_out));  // open: bin, bout
  assign and_1_out = A & B;  // AND_Gate and_1, 8 bits wide
  assign or_1_out = A | B;  // OR_Gate or_1, 8 bits wide
  assign xor_1_out = A ^ B;  // XOR_Gate xor_1, 8 bits wide
  assign nand_1_out = ~(A & B);  // NAND_Gate nand_1, 8 bits wide
  assign nor_1_out = ~(A | B);  // NOR_Gate nor_1, 8 bits wide
  assign xnor_1_out = ~(A ^ B);  // XNOR_Gate xnor_1, 8 bits wide
  Multiplexer #(.select(3), .width(8)) multiplexer_1 (
    .in0(adder_1_out), .in1(subtractor_1_out), .in2(and_1_out), .in3(or_1_out), .in4(xor_1_out),
    .in5(nand_1_out), .in6(nor_1_out), .in7(xnor_1_out), .out(SAIDA), .sel(SELETOR));

  // Notes on the sheet:
  //   ENTRADA
  //   MULTIPLEXADOR
endmodule

module ULA_Principal (
  input  [7:0] A,
  input  [7:0] B,
  input  [2:0] S,
  output [7:0] F
);

  wire [7:0] adder_1_out, and_1_out, nand_1_out, nor_1_out, or_1_out, subtractor_1_out, xnor_1_out, xor_1_out;

  Adder adder_1 (.a(A), .b(B), .out(adder_1_out));  // open: cin, cout
  Subtractor subtractor_1 (.a(A), .b(B), .out(subtractor_1_out));  // open: bin, bout
  assign and_1_out = A & B;  // AND_Gate and_1, 8 bits wide
  assign or_1_out = A | B;  // OR_Gate or_1, 8 bits wide
  assign xor_1_out = A ^ B;  // XOR_Gate xor_1, 8 bits wide
  assign nand_1_out = ~(A & B);  // NAND_Gate nand_1, 8 bits wide
  assign nor_1_out = ~(A | B);  // NOR_Gate nor_1, 8 bits wide
  assign xnor_1_out = ~(A ^ B);  // XNOR_Gate xnor_1, 8 bits wide
  Multiplexer #(.select(3), .width(8)) multiplexer_1 (
    .in0(adder_1_out), .in1(subtractor_1_out), .in2(and_1_out), .in3(or_1_out), .in4(xor_1_out),
    .in5(nand_1_out), .in6(nor_1_out), .in7(xnor_1_out), .out(F), .sel(S));

  // Notes on the sheet:
  //   ENTRADA
  //   PROJETO DE UMA UNIDADE LÓGICA ARITIMÉTICA (ULA) 
  //   MULTIPLEXADOR
  //   8 X 1
  //   SELETOR
  //   SAIDA
endmodule
